// Logisim project Semanal3.circ as structural Verilog: 2 circuits, main circuit Ejercicio1
module Ejercicio1 (
  input  W,
  input  X,
  input  Y,
  input  Z
);

  wire NOT_W_out, NOT_W_Y_out, NOT_Z_out, or_1_out, W_NOT_Z_out;

  not NOT_W (NOT_W_out, W);
  not NOT_Z (NOT_Z_out, Z);
  and NOT_W_Y (NOT_W_Y_out, NOT_W_out, Y);
  and W_NOT_Z (W_NOT_Z_out, W, NOT_Z_out);
  or or_1 (or_1_out, NOT_W_Y_out, X, W_NOT_Z_out);
  LED led_1 (.in(or_1_out));

  // Notes on the sheet:
  //   X + ((NOT W)Y) + (W(NOT Z))
endmodule

module Ejercicio2 (
  input  A,
  input  B,
  input  C,
  input  D
);

  wire B_NOT_C_D_out, NOT_A__NOT_B_C_out, NOT_A_BD_out, NOT_A_out, NOT_B_CD_out, NOT_B_out, NOT_C_out,
       or_1_out;

  not NOT_A (NOT_A_out, A);
  not NOT_B (NOT_B_out, B);
  not NOT_C (NOT_C_out, C);
  and NOT_A__NOT_B_C (NOT_A__NOT_B_C_out, NOT_A_out, NOT_B_out, C);
  and NOT_B_CD (NOT_B_CD_out, NOT_B_out, C, D);
  and NOT_A_BD (NOT_A_BD_out, NOT_A_out, B, D);
  and B_NOT_C_D (B_NOT_C_D_out, B, NOT_C_out, D);
  or or_1 (or_1_out, NOT_A__NOT_B_C_out, NOT_B_CD_out, NOT_A_BD_out, B_NOT_C_D_out);
  LED led_1 (.in(or_1_out));

  // Notes on the sheet:
  //   (NOT A)(NOT B)C + (NOT B)CD + (NOT A)BD + B(NOT C)D
endmodule
